// Logisim project Add.circ as structural Verilog: 1 circuit, main circuit main
module main (
  input  in_1,
  input  in_2,
  input  in_3,
  input  in_4,
  output out_5,
  output out_6
);

  Adder #(.width(2)) adder_1 (.a({in_2, in_1}), .b({in_3, in_4}), .out({out_6, out_5}));  // open: cin, cout
endmodule
