// Logisim project Counter4.circ as structural Verilog: 1 circuit, main circuit main
module main (
  input  INC,
  input  CLR,
  output C4,
  output C3,
  output C2,
  output C1
);

  wire and_1_out, and_2_out, and_3_out, CLK_out, or_1_out, or_2_out, or_3_out, or_4_out;

  Clock CLK (.out(CLK_out));
  or or_1 (or_1_out, and_1_out, CLR);
  and and_1 (and_1_out, and_2_out, C3);
  or or_2 (or_2_out, and_2_out, CLR);
  J_K_Flip_Flop j_k_ff_1 (.J(and_1_out), .clk(CLK_out), .K(or_1_out), .Q(C4));  // open: Qn, preset, en, reset
  and and_2 (and_2_out, and_3_out, C2);
  or or_3 (or_3_out, and_3_out, CLR);
  J_K_Flip_Flop j_k_ff_2 (.J(and_2_out), .clk(CLK_out), .K(or_2_out), .Q(C3));  // open: Qn, preset, en, reset
  J_K_Flip_Flop j_k_ff_3 (.J(and_3_out), .clk(CLK_out), .K(or_3_out), .Q(C2));  // open: Qn, preset, en, reset
  and and_3 (and_3_out, INC, C1);
  or or_4 (or_4_out, INC, CLR);
  J_K_Flip_Flop j_k_ff_4 (.J(INC), .clk(CLK_out), .K(or_4_out), .Q(C1));  // open: Qn, preset, en, reset

  // Notes on the sheet:
  //   4-Bit Counter
  //   Change state on PGT of CLK
endmodule
