// Logisim project DFF.circ as structural Verilog: 1 circuit, main circuit main
module main (
  input  D,
  input  Clock,
  output Q,
  output Q_prime
);

  wire and_1_out, and_2_out, and_3_out, and_4_out, nor_1_out, nor_2_out, not_1_out, not_2_out;

  not not_1 (not_1_out, D);
  not not_2 (not_2_out, Clock);
  and and_1 (and_1_out, D, not_2_out);
  and and_2 (and_2_out, not_1_out, not_2_out);
  nor nor_1 (nor_1_out, and_1_out, nor_2_out);
  nor nor_2 (nor_2_out, nor_1_out, and_2_out);
  and and_3 (and_3_out, Clock, nor_1_out);
  and and_4 (and_4_out, nor_2_out, Clock);
  nor nor_3 (Q, and_3_out, Q_prime);
  nor nor_4 (Q_prime, Q, and_4_out);

  // Notes on the sheet:
  //   Input Latch
  //   Master-Slave D Flip Flop
  //   Output Latch
endmodule
