// Logisim project Decoder.circ as structural Verilog: 1 circuit, main circuit main
module main (
  input  S2,
  input  S1,
  output Out0,
  output Out1,
  output Out2,
  output Out3
);

  wire not_1_out, not_2_out;

  not not_1 (not_1_out, S2);
  not not_2 (not_2_out, S1);
  and and_1 (Out0, not_2_out, not_1_out);
  and and_2 (Out1, S1, not_1_out);
  and and_3 (Out2, not_2_out, S2);
  and and_4 (Out3, S1, S2);

  // Notes on the sheet:
  //   Decoder
endmodule
