// Logisim project RSEnable.circ as structural Verilog: 1 circuit, main circuit main
module main (
  input  R,
  input  Enable,
  input  S,
  output Q,
  output Q_prime
);

  wire and_1_out, and_2_out;

  and and_1 (and_1_out, R, Enable);
  and and_2 (and_2_out, Enable, S);
  nor nor_1 (Q, and_1_out, Q_prime);
  nor nor_2 (Q_prime, Q, and_2_out);

  // Notes on the sheet:
  //   RS Latch with Enable
endmodule
