// Logisim project Ripple4.circ as structural Verilog: 1 circuit, main circuit main
module main (
  output out_1,
  output out_2,
  output out_3,
  output out_4,
  output out_5,
  output out_6,
  output out_7,
  output out_8
);

  wire clock_1_out;

  Clock clock_1 (.out(clock_1_out));
  J_K_Flip_Flop j_k_ff_1 (.J(1'b1), .clk(clock_1_out), .K(1'b1), .Q(out_1), .Qn(out_5));  // open: preset, en, reset
  J_K_Flip_Flop j_k_ff_2 (.J(1'b1), .clk(out_5), .K(1'b1), .Q(out_2), .Qn(out_6));  // open: preset, en, reset
  J_K_Flip_Flop j_k_ff_3 (.J(1'b1), .clk(out_6), .K(1'b1), .Q(out_3), .Qn(out_7));  // open: preset, en, reset
  J_K_Flip_Flop j_k_ff_4 (.J(1'b1), .clk(out_7), .K(1'b1), .Q(out_4), .Qn(out_8));  // open: preset, en, reset

  // Notes on the sheet:
  //   4-Bit Up-Down Ripple Counter
endmodule
