// Logisim project counter.circ as structural Verilog: 1 circuit, main circuit main
module main (
  input  in_1,
  output out_2
);

  wire clock_1_out;
  wire [22:0] counter_1_q;

  Clock clock_1 (.out(clock_1_out));
  Counter #(.width(24), .max('hffffff)) counter_1 (
    .count(in_1), .Q({out_2, counter_1_q}), .clk(clock_1_out));  // open: load, D, carry, clr
endmodule
