// Logisim project Multiplexer.circ as structural Verilog: 1 circuit, main circuit main
module main (
  input  S2,
  input  S1,
  input  In0,
  input  In1,
  input  In2,
  input  In3,
  output Out
);

  wire and_1_out, and_2_out, and_3_out, and_4_out, not_1_out, not_2_out;

  not not_1 (not_1_out, S2);
  not not_2 (not_2_out, S1);
  and and_1 (and_1_out, not_2_out, In0, not_1_out);
  and and_2 (and_2_out, S1, In1, not_1_out);
  and and_3 (and_3_out, not_2_out, In2, S2);
  and and_4 (and_4_out, S1, In3, S2);
  or or_1 (Out, and_1_out, and_2_out, and_3_out, and_4_out);

  // Notes on the sheet:
  //   Multiplexer
endmodule
