// Logisim project RSLatchNAnd.circ as structural Verilog: 1 circuit, main circuit main
module main (
  input  S,
  input  R,
  output Q,
  output Q_prime
);

  nand nand_1 (Q, S, Q_prime);
  nand nand_2 (Q_prime, Q, R);

  // Notes on the sheet:
  //   RS Latch
endmodule
