// Logisim project SRFF.circ as structural Verilog: 1 circuit, main circuit main
module main (
  input  in_1,
  input  in_2,
  output out_3
);

  wire clock_1_out;

  Clock clock_1 (.out(clock_1_out));
  S_R_Flip_Flop s_r_ff_1 (.S(in_1), .clk(clock_1_out), .R(in_2), .Q(out_3));  // open: Qn, preset, reset, en
endmodule
