// Logisim project register.circ as structural Verilog: 1 circuit, main circuit main
module main (
  input  in_1,
  input  in_2,
  output out_3,
  output out_4
);

  wire clock_1_out;

  Clock clock_1 (.out(clock_1_out));
  Register #(.width(2)) register_1 (.D({in_2, in_1}), .Q({out_4, out_3}), .clk(clock_1_out));  // open: en, clr
endmodule
