// Logisim project splitter.circ as structural Verilog: 1 circuit, main circuit main
module main (
  input  in_1,
  input  in_2,
  output out_3,
  output out_4
);


  assign out_3 = in_2;
  assign out_4 = in_1;
endmodule
