// Logisim project updown.circ as structural Verilog: 1 circuit, main circuit main
module main (
  input  in_1,
  output out_2,
  output out_3,
  output out_4,
  output out_5
);

  wire and_1_out, and_2_out, and_3_out, and_4_out, and_5_out, and_6_out, clock_1_out, not_1_out, or_1_out,
       or_2_out, or_3_out;

  Clock clock_1 (.out(clock_1_out));
  T_Flip_Flop t_ff_1 (.clk(clock_1_out), .T(1'b1), .Q(out_2));  // open: Qn, preset, reset, en
  not not_1 (not_1_out, in_1);
  and and_1 (and_1_out, in_1, out_2);
  and and_2 (and_2_out, ~out_2, not_1_out);  // AND_Gate
  T_Flip_Flop t_ff_2 (.clk(clock_1_out), .T(or_1_out), .Q(out_3));  // open: Qn, preset, reset, en
  or or_1 (or_1_out, and_1_out, and_2_out);
  and and_3 (and_3_out, and_1_out, out_3);
  and and_4 (and_4_out, ~out_3, and_2_out);  // AND_Gate
  T_Flip_Flop t_ff_3 (.clk(clock_1_out), .T(or_2_out), .Q(out_4));  // open: Qn, preset, reset, en
  or or_2 (or_2_out, and_3_out, and_4_out);
  and and_5 (and_5_out, and_3_out, out_4);
  and and_6 (and_6_out, ~out_4, and_4_out);  // AND_Gate
  T_Flip_Flop t_ff_4 (.clk(clock_1_out), .T(or_3_out), .Q(out_5));  // open: Qn, preset, reset, en
  or or_3 (or_3_out, and_5_out, and_6_out);
endmodule
